# Fritzing sketch Chronograph (saved by Fritzing 0.9.10b)
breadboards: 1

parts:
  Part1 = Arduino Uno (Rev3)
  LCD1 = LCD screen
  S1 = Toggle Switch [package=THT]
  VCC1 = Battery block 9V
  R1 = Resistor [tolerance=±5% power=0.25 resistance=220 package=THT]
  HC-SR04_Sensor_1 = HC-SR04 Ultrasonic Distance Sensor
  HC-SR04_Sensor_2 = HC-SR04 Ultrasonic Distance Sensor
  R2 = Rotary Potentiometer (Small) [maximum_resistance=100kΩ knob_status=50% power=0.5W package=THT]

nets:
  N1: Part1.D8, HC-SR04_Sensor_2.ECHO
  N2: Part1.D9_PWM, HC-SR04_Sensor_2.TRIG
  N3: Part1.D10_PWM/SS, HC-SR04_Sensor_1.ECHO
  N4: Part1.D11_PWM/MOSI, HC-SR04_Sensor_1.TRIG
  GND: Part1.GND, LCD1.VSS, LCD1.R/W, LCD1.LED-, VCC1.-, HC-SR04_Sensor_1.GND, HC-SR04_Sensor_2.GND, R2.leg2
  N5: Part1.D2, LCD1.RS
  N6: Part1.D3_PWM, LCD1.E
  N7: Part1.D4, LCD1.DB4
  N8: Part1.D5_PWM, LCD1.DB5
  N9: Part1.D6_PWM, LCD1.DB6
  N10: Part1.D7, LCD1.DB7
  VCC: Part1.5V, LCD1.VDD, R1.Pin_1, HC-SR04_Sensor_1.VCC, HC-SR04_Sensor_2.VCC, R2.leg1
  N11: Part1.VIN, S1.COM
  N12: LCD1.V0, R2.wiper
  N13: LCD1.LED+, R1.Pin_0
  N14: S1.L1, VCC1.+
